// Logisim project main.circ as structural Verilog: 11 circuits, main circuit main
module main (
  input  [7:0] birth_input,
  input  [7:0] survival_input
);

  wire and_1_out, and_2_out, and_3_out, and_4_out, and_5_out, and_6_out, and_7_out, and_8_out, and_10_out,
       and_11_out, and_13_out, and_14_out, cdm_8_mark5_1_p1, cdm_8_mark5_1_p2, cdm_8_mark5_1_p4,
       cdm_8_mark5_1_p5, cdm_8_mark5_1_p6, cdm_8_mark5_1_p7, cdm_8_mark5_1_p8, cdm_8_mark5_1_p9, change_bit,
       change_bit_slow, clock, code, comparator_1_eq, comparator_2_eq, comparator_3_eq, comparator_4_eq,
       comparator_5_eq, comparator_6_eq, comparator_7_eq, comparator_8_eq, comparator_9_eq, comparator_10_eq,
       comparator_11_eq, comparator_12_eq, comparator_13_lt, comparator_14_eq, comparator_15_eq, data,
       decoder_1_out0, decoder_3_out0, decoder_4_out1, decoder_5_out0, decoder_5_out1, decoder_6_out0,
       decoder_7_out1, decoder_8_out0, decoder_8_out1, decoder_9_out1, decoder_11_out0, decoder_11_out1,
       decoder_12_out0, decoder_12_out1, in_out, IOsel, mem, multiplexer_3_out,
       n32_bit_row_destructor_1_selected_bit, not_1_out, not_2_out, not_3_out, not_4_out, not_5_out,
       not_6_out, not_8_out, not_11_out, not_12_out, not_13_out, not_14_out, not_15_out, not_17_out,
       not_18_out, not_19_out, not_20_out, not_21_out, not_23_out, not_24_out, not_25_out, not_26_out,
       or_1_out, or_2_out, or_3_out, or_4_out, playing, RAM, recieve_row, recieve_row_slow, send_row,
       send_row_slow, setting, undriven_3, xnor_1_out, xnor_2_out, xnor_3_out;
  wire [4:0] cpuX, cpuY, keyboard_controller_1_x, keyY, multiplexer_2_out;
  wire [6:0] keyboard_1_data;
  wire [7:0] bus, cdm_8_mark5_1_p13, cdm_8_mark5_1_p14, controlled_buffer_4_out, controlled_buffer_6_out,
       controlled_buffer_10_out, controlled_buffer_16_out, controlled_buffer_20_out, IOaddr, not_22_out,
       register_1_q, register_5_q, register_7_q, register_8_q, register_9_q, register_10_q, register_11_q,
       start, undriven_2;
  wire [7:1] register_3_q;
  wire [7:5] register_2_q, register_6_q;
  wire [15:8] cdm_8_mark5_1_p12;
  wire [31:0] bit_invertor_1_changed_string, bit_invertor_1_output1, bit_invertor_1_output2,
       bit_invertor_1_output3, bit_invertor_1_output4, bit_invertor_1_output5, bit_invertor_1_output6,
       bit_invertor_1_output7, bit_invertor_1_output8, bit_invertor_1_output9, bit_invertor_1_output10,
       bit_invertor_1_output11, bit_invertor_1_output12, bit_invertor_1_output13, bit_invertor_1_output14,
       bit_invertor_1_output15, bit_invertor_1_output16, bit_invertor_1_output17_2, bit_invertor_1_output18,
       bit_invertor_1_output19, bit_invertor_1_output20, bit_invertor_1_output21, bit_invertor_1_output22,
       bit_invertor_1_output23, bit_invertor_1_output24, bit_invertor_1_output25, bit_invertor_1_output26,
       bit_invertor_1_output27, bit_invertor_1_output28, bit_invertor_1_output29, bit_invertor_1_output30,
       bit_invertor_1_output31, bit_invertor_1_output32, cpuRow, inverted_row, multiplexer_1_out,
       n32_32_buffer_1_row_0, n32_32_buffer_1_row_1, n32_32_buffer_1_row_2_2, n32_32_buffer_1_row_3,
       n32_32_buffer_1_row_4, n32_32_buffer_1_row_4_2, n32_32_buffer_1_row_5, n32_32_buffer_1_row_6_2,
       n32_32_buffer_1_row_7, n32_32_buffer_1_row_8_2, n32_32_buffer_1_row_10, n32_32_buffer_1_row_11,
       n32_32_buffer_1_row_12, n32_32_buffer_1_row_13, n32_32_buffer_1_row_15, n32_32_buffer_1_row_15_2,
       n32_32_buffer_1_row_17, n32_32_buffer_1_row_18, n32_32_buffer_1_row_19, n32_32_buffer_1_row_20,
       n32_32_buffer_1_row_21, n32_32_buffer_1_row_22, n32_32_buffer_1_row_23, n32_32_buffer_1_row_24,
       n32_32_buffer_1_row_25, n32_32_buffer_1_row_26, n32_32_buffer_1_row_28, n32_32_buffer_1_row_29,
       n32_32_buffer_1_row_29_2, n32_32_buffer_1_row_30, n32_32_buffer_1_row_31,
       n32_32_buffer_1_selected_row_output, row_reverser_1_reversed_row, row_reverser_2_reversed_row,
       row_reverser_3_reversed_row, row_reverser_4_reversed_row, row_reverser_5_reversed_row,
       row_reverser_6_reversed_row, row_reverser_7_reversed_row, row_reverser_8_reversed_row,
       row_reverser_9_reversed_row, row_reverser_10_reversed_row, row_reverser_11_reversed_row,
       row_reverser_12_reversed_row, row_reverser_13_reversed_row, row_reverser_14_reversed_row,
       row_reverser_15_reversed_row, row_reverser_16_reversed_row, row_reverser_17_reversed_row,
       row_reverser_18_reversed_row, row_reverser_19_reversed_row, row_reverser_20_reversed_row,
       row_reverser_21_reversed_row, row_reverser_22_reversed_row, row_reverser_23_reversed_row,
       row_reverser_24_reversed_row, row_reverser_25_reversed_row, row_reverser_26_reversed_row,
       row_reverser_27_reversed_row, row_reverser_28_reversed_row, row_reverser_29_reversed_row,
       row_reverser_30_reversed_row, row_reverser_31_reversed_row, row_reverser_32_reversed_row, undriven;

  Keyboard keyboard_1 (.clk(clock), .re(setting), .data(keyboard_1_data));  // open: clr, avail
  Button u_Start (.out(start[0]));
  Keyboard_controller keyboard_controller_1 (
    .ASCII_code(keyboard_1_data), .X(keyboard_controller_1_x), .Switch(change_bit));
  not not_1 (not_1_out, not_1_out);
  not not_2 (not_2_out, not_2_out);
  not not_3 (not_3_out, not_3_out);
  not not_4 (not_4_out, not_4_out);
  Multiplexer #(.width(32), .disabled(0), .enable("false")) multiplexer_1 (
    .in0(inverted_row), .in1(cpuRow), .out(multiplexer_1_out), .sel(playing));
  Multiplexer #(.width(5), .disabled(0), .enable("false")) multiplexer_2 (
    .in0(keyY), .in1(cpuY), .out(multiplexer_2_out), .sel(playing));
  Multiplexer #(.disabled(0), .enable("false")) multiplexer_3 (
    .in0(change_bit), .in1(send_row_slow), .out(multiplexer_3_out), .sel(playing));
  // Probe on keyY
  // Probe on keyboard_controller_1_x
  not not_5 (not_5_out, change_bit);
  not not_6 (not_6_out, send_row);
  not not_7 (send_row_slow, not_6_out);
  not not_8 (not_8_out, recieve_row);
  not not_9 (recieve_row_slow, not_8_out);
  _32_32_buffer u_32_32_buffer_1 (
    .Row_0(n32_32_buffer_1_row_0), .Row_1(n32_32_buffer_1_row_1), .Row_2_2(n32_32_buffer_1_row_2_2),
    .Row_3(n32_32_buffer_1_row_3), .Row_4(n32_32_buffer_1_row_4), .Row_5(n32_32_buffer_1_row_5),
    .Row_6_2(n32_32_buffer_1_row_6_2), .Row_7(n32_32_buffer_1_row_7), .Row_8_2(n32_32_buffer_1_row_8_2),
    .Row_4_2(n32_32_buffer_1_row_4_2), .Row_10(n32_32_buffer_1_row_10), .Row_11(n32_32_buffer_1_row_11),
    .Row_12(n32_32_buffer_1_row_12), .Row_13(n32_32_buffer_1_row_13), .Row_15(n32_32_buffer_1_row_15),
    .Row_15_2(n32_32_buffer_1_row_15_2), .Row_29(n32_32_buffer_1_row_29), .Row_17(n32_32_buffer_1_row_17),
    .Row_18(n32_32_buffer_1_row_18), .Row_19(n32_32_buffer_1_row_19), .Row_20(n32_32_buffer_1_row_20),
    .Row_21(n32_32_buffer_1_row_21), .Row_22(n32_32_buffer_1_row_22), .Row_23(n32_32_buffer_1_row_23),
    .Row_24(n32_32_buffer_1_row_24), .Row_25(n32_32_buffer_1_row_25), .Row_26(n32_32_buffer_1_row_26),
    .Row_28(n32_32_buffer_1_row_28), .Row_29_2(n32_32_buffer_1_row_29_2), .Row_30(n32_32_buffer_1_row_30),
    .Row_31(n32_32_buffer_1_row_31), .Row_selector(multiplexer_2_out), .Write_row(multiplexer_3_out),
    .clock(clock), .Selected_row_output(n32_32_buffer_1_selected_row_output));
  not not_10 (change_bit_slow, not_5_out);
  not not_11 (not_11_out, start[0]);
  Register register_1 (.D(bus), .Q(register_1_q), .clk(not_13_out));  // open: en, clr
  not not_12 (not_12_out, decoder_1_out0);
  not not_13 (not_13_out, not_12_out);
  assign bus = recieve_row ? {8{1'b0}} : 8'bz;  // Controlled_Buffer controlled_buffer_1
  Register register_2 (.D(start), .Q({register_2_q, cpuY}), .clk(not_14_out));  // open: en, clr
  not not_14 (not_14_out, not_15_out);
  Register register_3 (.D(8'h1), .Q({register_3_q, playing}), .clk(xnor_1_out));  // open: en, clr
  xnor xnor_1 (xnor_1_out, not_11_out, start[0]);
  assign cpuRow = recieve_row ? n32_32_buffer_1_selected_row_output : 32'bz;  // Controlled_Buffer controlled_buffer_2
  _32_bit_row_destructor u_32_bit_row_destructor_1 (
    .Row(n32_32_buffer_1_selected_row_output), .Bit_selector(keyboard_controller_1_x),
    .Selected_bit(n32_bit_row_destructor_1_selected_bit));  // open: Selected_byte
  Decoder #(.disabled(0)) decoder_1 (.out0(decoder_1_out0), .sel(recieve_row_slow), .en(and_2_out));  // open: out1
  Decoder #(.disabled(0)) decoder_2 (.out0(send_row), .out1(recieve_row), .sel(in_out), .en(and_3_out));
  Decoder #(.disabled(0)) decoder_3 (.out0(decoder_3_out0), .sel(in_out), .en(and_4_out));  // open: out1
  not not_15 (not_15_out, decoder_3_out0);
  Decoder #(.disabled(0)) decoder_4 (.out1(decoder_4_out1), .sel(in_out), .en(and_5_out));  // open: out0
  assign bus = decoder_4_out1 ? {register_3_q, playing} : 8'bz;  // Controlled_Buffer controlled_buffer_3
  LED led_1 (.in(n32_bit_row_destructor_1_selected_bit));
  and and_1 (and_1_out, clock, setting);
  Comparator comparator_1 (.a(IOaddr), .b(8'hfa), .eq(comparator_1_eq));  // open: gt, lt
  and and_2 (and_2_out, comparator_1_eq, IOsel);
  Comparator comparator_2 (.a(IOaddr), .b(8'hf5), .eq(comparator_2_eq));  // open: gt, lt
  and and_3 (and_3_out, comparator_2_eq, IOsel);
  Comparator comparator_3 (.a(IOaddr), .b(8'hf3), .eq(comparator_3_eq));  // open: gt, lt
  and and_4 (and_4_out, comparator_3_eq, IOsel);
  Comparator comparator_4 (.a(IOaddr), .b(8'hf0), .eq(comparator_4_eq));  // open: gt, lt
  and and_5 (and_5_out, comparator_4_eq, IOsel);
  not not_16 (setting, playing);
  bit_invertor bit_invertor_1 (
    .INPUT9(n32_32_buffer_1_row_8_2), .INPUT1(n32_32_buffer_1_row_0), .INPUT10(n32_32_buffer_1_row_4_2),
    .INPUT17(n32_32_buffer_1_row_29), .INPUT2(n32_32_buffer_1_row_1), .INPUT31(n32_32_buffer_1_row_10),
    .INPUT18(n32_32_buffer_1_row_17), .INPUT25(n32_32_buffer_1_row_24), .INPUT3(n32_32_buffer_1_row_2_2),
    .INPUT12(n32_32_buffer_1_row_11), .INPUT19(n32_32_buffer_1_row_18), .INPUT26(n32_32_buffer_1_row_25),
    .INPUT4(n32_32_buffer_1_row_3), .SWITCH(and_1_out), .INPUT13(n32_32_buffer_1_row_12),
    .INPUT20(n32_32_buffer_1_row_19), .INPUT27(n32_32_buffer_1_row_26), .Y(keyY),
    .INPUT5(n32_32_buffer_1_row_4), .X(keyboard_controller_1_x), .INPUT14(n32_32_buffer_1_row_13),
    .INPUT21(n32_32_buffer_1_row_20), .INPUT28(undriven), .INPUT6(n32_32_buffer_1_row_5),
    .INPUT15(n32_32_buffer_1_row_15), .INPUT22(n32_32_buffer_1_row_21), .INPUT29(n32_32_buffer_1_row_28),
    .INPUT7(n32_32_buffer_1_row_6_2), .INPUT16(n32_32_buffer_1_row_15_2), .INPUT23(n32_32_buffer_1_row_22),
    .INPUT30(n32_32_buffer_1_row_29_2), .INPUT8(n32_32_buffer_1_row_7), .INPUT24(n32_32_buffer_1_row_23),
    .INPUT31_2(n32_32_buffer_1_row_30), .CHANGED_STRING(bit_invertor_1_changed_string),
    .OUTPUT1(bit_invertor_1_output1), .OUTPUT2(bit_invertor_1_output2), .OUTPUT3(bit_invertor_1_output3),
    .OUTPUT4(bit_invertor_1_output4), .OUTPUT5(bit_invertor_1_output5), .OUTPUT6(bit_invertor_1_output6),
    .OUTPUT7(bit_invertor_1_output7), .OUTPUT8(bit_invertor_1_output8), .OUTPUT9(bit_invertor_1_output9),
    .OUTPUT10(bit_invertor_1_output10), .OUTPUT11(bit_invertor_1_output11),
    .OUTPUT12(bit_invertor_1_output12), .OUTPUT13(bit_invertor_1_output13),
    .OUTPUT14(bit_invertor_1_output14), .OUTPUT15(bit_invertor_1_output15),
    .OUTPUT16(bit_invertor_1_output16), .OUTPUT17_2(bit_invertor_1_output17_2),
    .OUTPUT18(bit_invertor_1_output18), .OUTPUT19(bit_invertor_1_output19),
    .OUTPUT20(bit_invertor_1_output20), .OUTPUT21(bit_invertor_1_output21),
    .OUTPUT22(bit_invertor_1_output22), .OUTPUT23(bit_invertor_1_output23),
    .OUTPUT24(bit_invertor_1_output24), .OUTPUT25(bit_invertor_1_output25),
    .OUTPUT26(bit_invertor_1_output26), .OUTPUT27(bit_invertor_1_output27),
    .OUTPUT28(bit_invertor_1_output28), .OUTPUT29(bit_invertor_1_output29),
    .OUTPUT30(bit_invertor_1_output30), .OUTPUT31(bit_invertor_1_output31), .OUTPUT32(bit_invertor_1_output32));
  not not_17 (not_17_out, and_1_out);
  Register #(.width(32)) register_4 (
    .D(bit_invertor_1_changed_string), .Q(inverted_row), .clk(not_17_out));  // open: en, clr
  not not_18 (not_18_out, not_18_out);
  not not_19 (not_19_out, not_19_out);
  row_reverser row_reverser_1 (.row(bit_invertor_1_output1), .reversed_row(row_reverser_1_reversed_row));
  row_reverser row_reverser_2 (.row(bit_invertor_1_output2), .reversed_row(row_reverser_2_reversed_row));
  row_reverser row_reverser_3 (.row(bit_invertor_1_output3), .reversed_row(row_reverser_3_reversed_row));
  row_reverser row_reverser_4 (.row(bit_invertor_1_output4), .reversed_row(row_reverser_4_reversed_row));
  row_reverser row_reverser_5 (.row(bit_invertor_1_output5), .reversed_row(row_reverser_5_reversed_row));
  row_reverser row_reverser_6 (.row(bit_invertor_1_output6), .reversed_row(row_reverser_6_reversed_row));
  row_reverser row_reverser_7 (.row(bit_invertor_1_output7), .reversed_row(row_reverser_7_reversed_row));
  row_reverser row_reverser_8 (.row(bit_invertor_1_output8), .reversed_row(row_reverser_8_reversed_row));
  row_reverser row_reverser_9 (.row(bit_invertor_1_output9), .reversed_row(row_reverser_9_reversed_row));
  row_reverser row_reverser_10 (.row(bit_invertor_1_output10), .reversed_row(row_reverser_10_reversed_row));
  row_reverser row_reverser_11 (.row(bit_invertor_1_output11), .reversed_row(row_reverser_11_reversed_row));
  row_reverser row_reverser_12 (.row(bit_invertor_1_output12), .reversed_row(row_reverser_12_reversed_row));
  row_reverser row_reverser_13 (.row(bit_invertor_1_output13), .reversed_row(row_reverser_13_reversed_row));
  row_reverser row_reverser_14 (.row(bit_invertor_1_output14), .reversed_row(row_reverser_14_reversed_row));
  row_reverser row_reverser_15 (.row(bit_invertor_1_output15), .reversed_row(row_reverser_15_reversed_row));
  row_reverser row_reverser_16 (.row(bit_invertor_1_output16), .reversed_row(row_reverser_16_reversed_row));
  row_reverser row_reverser_17 (.row(bit_invertor_1_output17_2), .reversed_row(row_reverser_17_reversed_row));
  row_reverser row_reverser_18 (.row(bit_invertor_1_output18), .reversed_row(row_reverser_18_reversed_row));
  row_reverser row_reverser_19 (.row(bit_invertor_1_output19), .reversed_row(row_reverser_19_reversed_row));
  row_reverser row_reverser_20 (.row(bit_invertor_1_output20), .reversed_row(row_reverser_20_reversed_row));
  row_reverser row_reverser_21 (.row(bit_invertor_1_output21), .reversed_row(row_reverser_21_reversed_row));
  row_reverser row_reverser_22 (.row(bit_invertor_1_output22), .reversed_row(row_reverser_22_reversed_row));
  row_reverser row_reverser_23 (.row(bit_invertor_1_output23), .reversed_row(row_reverser_23_reversed_row));
  row_reverser row_reverser_24 (.row(bit_invertor_1_output24), .reversed_row(row_reverser_24_reversed_row));
  row_reverser row_reverser_25 (.row(bit_invertor_1_output25), .reversed_row(row_reverser_25_reversed_row));
  row_reverser row_reverser_26 (.row(bit_invertor_1_output26), .reversed_row(row_reverser_26_reversed_row));
  row_reverser row_reverser_27 (.row(bit_invertor_1_output27), .reversed_row(row_reverser_27_reversed_row));
  row_reverser row_reverser_28 (.row(bit_invertor_1_output28), .reversed_row(row_reverser_28_reversed_row));
  row_reverser row_reverser_29 (.row(bit_invertor_1_output29), .reversed_row(row_reverser_29_reversed_row));
  row_reverser row_reverser_30 (.row(bit_invertor_1_output30), .reversed_row(row_reverser_30_reversed_row));
  row_reverser row_reverser_31 (.row(bit_invertor_1_output31), .reversed_row(row_reverser_31_reversed_row));
  row_reverser row_reverser_32 (.row(bit_invertor_1_output32), .reversed_row(row_reverser_32_reversed_row));
  // Probe on inverted_row
  LED led_2 (.in(comparator_5_eq));
  Comparator comparator_5 (.a({8{1'b0}}), .b(register_1_q), .eq(comparator_5_eq));  // open: gt, lt
  LED led_3 (.in(comparator_6_eq));
  Comparator comparator_6 (.a(8'h41), .b(register_1_q), .eq(comparator_6_eq));  // open: gt, lt
  Comparator comparator_7 (.a(8'h42), .b(register_1_q), .eq(comparator_7_eq));  // open: gt, lt
  not not_20 (not_20_out, setting);
  DotMatrix #(.inputtype("row"), .matrixcols(32), .matrixrows(32)) dotmatrix_1 (
    .row0(row_reverser_1_reversed_row), .row1(row_reverser_2_reversed_row),
    .row2(row_reverser_3_reversed_row), .row3(row_reverser_4_reversed_row),
    .row4(row_reverser_5_reversed_row), .row5(row_reverser_6_reversed_row),
    .row6(row_reverser_7_reversed_row), .row7(row_reverser_8_reversed_row),
    .row8(row_reverser_9_reversed_row), .row9(row_reverser_10_reversed_row),
    .row10(row_reverser_11_reversed_row), .row11(row_reverser_12_reversed_row),
    .row12(row_reverser_13_reversed_row), .row13(row_reverser_14_reversed_row),
    .row14(row_reverser_15_reversed_row), .row15(row_reverser_16_reversed_row),
    .row16(row_reverser_17_reversed_row), .row17(row_reverser_18_reversed_row),
    .row18(row_reverser_19_reversed_row), .row19(row_reverser_20_reversed_row),
    .row20(row_reverser_21_reversed_row), .row21(row_reverser_22_reversed_row),
    .row22(row_reverser_23_reversed_row), .row23(row_reverser_24_reversed_row),
    .row24(row_reverser_25_reversed_row), .row25(row_reverser_26_reversed_row),
    .row26(row_reverser_27_reversed_row), .row27(row_reverser_28_reversed_row),
    .row28(row_reverser_29_reversed_row), .row29(row_reverser_30_reversed_row),
    .row30(row_reverser_31_reversed_row), .row31(row_reverser_32_reversed_row));
  LED led_4 (.in(comparator_7_eq));
  Controlled_Buffer #(.width(8), .value('h0)) controlled_buffer_4 (
    .in(bus), .out(controlled_buffer_4_out));  // open: en
  assign controlled_buffer_4_out = recieve_row ? cpuRow[7:0] : 8'bz;  // Controlled_Buffer controlled_buffer_5
  assign controlled_buffer_6_out = decoder_6_out0 ? start : 8'bz;  // Controlled_Buffer controlled_buffer_6
  xnor xnor_2 (xnor_2_out, not_20_out, setting);
  assign bus = decoder_5_out1 ? register_5_q : 8'bz;  // Controlled_Buffer controlled_buffer_7
  Register register_5 (.D(controlled_buffer_4_out), .Q(register_5_q), .clk(or_1_out));  // open: en, clr
  or or_1 (or_1_out, recieve_row_slow, decoder_5_out0);
  Register register_6 (.D(controlled_buffer_6_out), .Q({register_6_q, cpuX}), .clk(decoder_6_out0));  // open: en, clr
  assign bus = decoder_7_out1 ? register_7_q : 8'bz;  // Controlled_Buffer controlled_buffer_8
  Register register_7 (.D(birth_input), .Q(register_7_q), .clk(xnor_2_out));  // open: en, clr
  Decoder #(.disabled(0)) decoder_5 (.out0(decoder_5_out0), .out1(decoder_5_out1), .sel(in_out), .en(and_6_out));
  assign cpuRow[7:0] = send_row ? register_5_q : 8'bz;  // Controlled_Buffer controlled_buffer_9
  Decoder #(.disabled(0)) decoder_6 (.out0(decoder_6_out0), .sel(in_out), .en(and_7_out));  // open: out1
  Decoder #(.disabled(0)) decoder_7 (.out1(decoder_7_out1), .sel(in_out), .en(and_8_out));  // open: out0
  Comparator comparator_8 (.a(IOaddr), .b(8'hf6), .eq(comparator_8_eq));  // open: gt, lt
  and and_6 (and_6_out, comparator_8_eq, IOsel);
  Comparator comparator_9 (.a(IOaddr), .b(8'hf4), .eq(comparator_9_eq));  // open: gt, lt
  and and_7 (and_7_out, comparator_9_eq, IOsel);
  Comparator comparator_10 (.a(IOaddr), .b(8'hf1), .eq(comparator_10_eq));  // open: gt, lt
  and and_8 (and_8_out, comparator_10_eq, IOsel);
  not not_21 (not_21_out, not_21_out);
  assign controlled_buffer_10_out = decoder_8_out0 ? bus : 8'bz;  // Controlled_Buffer controlled_buffer_10
  assign controlled_buffer_10_out = recieve_row ? cpuRow[15:8] : 8'bz;  // Controlled_Buffer controlled_buffer_11
  or or_2 (or_2_out, recieve_row_slow, decoder_8_out0);
  assign bus = decoder_8_out1 ? register_8_q : 8'bz;  // Controlled_Buffer controlled_buffer_12
  Register register_8 (.D(controlled_buffer_10_out), .Q(register_8_q), .clk(or_2_out));  // open: en, clr
  assign not_22_out = ~survival_input;  // NOT_Gate not_22, 8 bits wide
  not not_23 (not_23_out, setting);
  Decoder #(.disabled(0)) decoder_8 (.out0(decoder_8_out0), .out1(decoder_8_out1), .sel(in_out), .en(and_10_out));
  assign cpuRow[15:8] = send_row ? register_8_q : 8'bz;  // Controlled_Buffer controlled_buffer_13
  Register register_9 (.D(not_22_out), .Q(register_9_q), .clk(xnor_3_out));  // open: en, clr
  xnor xnor_3 (xnor_3_out, not_23_out, setting);
  // Probe on cdm_8_mark5_1_p5
  // Probe on cdm_8_mark5_1_p1
  // Probe on cdm_8_mark5_1_p4
  // Probe on cdm_8_mark5_1_p2
  Clock clock_1 (.out(clock));
  and and_9 (IOsel, not_24_out, clock, data);
  Comparator comparator_11 (.a(IOaddr), .b(8'hf7), .eq(comparator_11_eq));  // open: gt, lt
  and and_10 (and_10_out, comparator_11_eq, IOsel);
  Decoder #(.disabled(0)) decoder_9 (.out1(decoder_9_out1), .sel(in_out), .en(and_11_out));  // open: out0
  assign bus = decoder_9_out1 ? register_9_q : 8'bz;  // Controlled_Buffer IOdata
  // Probe on cdm_8_mark5_1_p6
  // Probe on cdm_8_mark5_1_p7
  // Probe on cdm_8_mark5_1_p8
  // CdM_8_mark5 cdm_8_mark5_1: pin names not known; wires that end beside it: cdm_8_mark5_1_p1, cdm_8_mark5_1_p2, clock, cdm_8_mark5_1_p4, cdm_8_mark5_1_p5, cdm_8_mark5_1_p6, cdm_8_mark5_1_p7, cdm_8_mark5_1_p8, cdm_8_mark5_1_p9, mem, in_out, {cdm_8_mark5_1_p12, IOaddr}, cdm_8_mark5_1_p13, cdm_8_mark5_1_p14
  not not_24 (not_24_out, comparator_13_lt);
  Comparator comparator_12 (.a(IOaddr), .b(undriven_2), .eq(comparator_12_eq));  // open: gt, lt
  and and_11 (and_11_out, comparator_12_eq, IOsel);
  Decoder #(.disabled(0)) decoder_10 (.out0(code), .out1(data), .sel(cdm_8_mark5_1_p9), .en(mem));
  assign bus = not_25_out ? cdm_8_mark5_1_p13 : 8'bz;  // Controlled_Buffer controlled_buffer_14
  not not_25 (not_25_out, in_out);
  assign cdm_8_mark5_1_p14 = in_out ? bus : 8'bz;  // Controlled_Buffer controlled_buffer_15
  and and_12 (RAM, comparator_13_lt, data);
  assign controlled_buffer_16_out = decoder_11_out0 ? bus : 8'bz;  // Controlled_Buffer controlled_buffer_16
  assign controlled_buffer_16_out = recieve_row ? cpuRow[23:16] : 8'bz;  // Controlled_Buffer controlled_buffer_17
  or or_3 (or_3_out, recieve_row_slow, decoder_11_out0);
  Decoder #(.disabled(0)) decoder_11 (.out0(decoder_11_out0), .out1(decoder_11_out1), .sel(in_out), .en(and_13_out));
  assign bus = decoder_11_out1 ? register_10_q : 8'bz;  // Controlled_Buffer controlled_buffer_18
  Register register_10 (.D(controlled_buffer_16_out), .Q(register_10_q), .clk(or_3_out));  // open: en, clr
  // Probe on {cdm_8_mark5_1_p12, IOaddr}
  Comparator #(.mode("unsigned")) comparator_13 (.a(IOaddr), .b(8'hf0), .lt(comparator_13_lt));  // open: gt, eq
  Comparator comparator_14 (.a(IOaddr), .b(8'hf8), .eq(comparator_14_eq));  // open: gt, lt
  assign cpuRow[23:16] = send_row ? register_10_q : 8'bz;  // Controlled_Buffer controlled_buffer_19
  and and_13 (and_13_out, comparator_14_eq, IOsel);
  ROM #(.addrWidth(16)) rom_1 (.addr({cdm_8_mark5_1_p12, IOaddr}), .data(bus), .sel(code));
  RAM ram_1 (.addr(IOaddr), .data(bus), .sel(RAM), .clk(clock), .ld(in_out));  // open: clr
  assign controlled_buffer_20_out = undriven_3 ? cpuRow[31:24] : 8'bz;  // Controlled_Buffer controlled_buffer_20
  // Probe on bus
  assign controlled_buffer_20_out = decoder_12_out0 ? bus : 8'bz;  // Controlled_Buffer controlled_buffer_21
  Register register_11 (.D(controlled_buffer_20_out), .Q(register_11_q), .clk(or_4_out));  // open: en, clr
  or or_4 (or_4_out, recieve_row_slow, decoder_12_out0);
  Decoder #(.disabled(0)) decoder_12 (.out0(decoder_12_out0), .out1(decoder_12_out1), .sel(in_out), .en(and_14_out));
  assign bus = decoder_12_out1 ? register_11_q : 8'bz;  // Controlled_Buffer controlled_buffer_22
  Comparator comparator_15 (.a(IOaddr), .b(8'hf9), .eq(comparator_15_eq));  // open: gt, lt
  assign cpuRow[31:24] = send_row ? register_11_q : 8'bz;  // Controlled_Buffer controlled_buffer_23
  and and_14 (and_14_out, comparator_15_eq, IOsel);
  not not_26 (not_26_out, not_26_out);
  // Pins of 1 and 8 bits meet at start

  // Other names for the same wires on the sheet: RAMAddr[7:0] = IOaddr; birth_cond[7:0] = birth_input;
  //   IOdata[7:0] = bus; rd_wr = in_out; survival_cond[7:0] = survival_input

  // Notes on the sheet:
  //   DEV I/O REGS.
  //   Keyboard
  //   ROW READ / WRITE
  //   (read only thus CdM -> buffer)
  //   PROCESSED CELL
  //   READ ONLY INPUTS
  //   (immutable game state)
  //   Cell 0xfa (CPU status)
  //   Cell 0xf3 (Y - row)
  //   Cell 0xf5 (row data direction)
  //   Cell 0xf0 (state)
  //   waiting for start
  //   reading field
  //   processing field
  //   Cells 0xf6-0xf9
  //   (little endtian row's bytes)
  //   Cell 0xf4 (X - bit)
  //   Cell 0xf1 (birth conditions)
  //   Cell 0xf2 (survival conditions)
  //   Structure of I/O bus
  //   Harvard Architecture
  //   Minimal IO cell address
  //   contents of rom_1 (hex, n*v repeats v):
  //   e0 4 dd 0 1 251*0 cd 40 d0 fa d1 40 a1 d1 f0 b4 0 e0 fd d1 f1 b4 d1 41 a4 d1 f2 b4 d1 42 a4 d0 fa d1
  //   41 a1 d0 ef d3 1f d1 f3 a7 d1 f5 b5 d1 f9 b6 a2 88 89 d2 f6 76 ea f8 8b ea ed d0 fa d1 42 a1 d0 1f
  //   d2 50 a8 d1 3 d2 51 a9 d2 80 d3 4 c2 c3 d0 50 b0 d1 51 b5 d3 60 d2 3 c2 c0 d2 70 94 94 18 14 b0 ac
  //   c4 c6 8a e1 d 8c d2 1f 48 d1 51 b5 d2 3 c2 ee 6 c2 8d d2 3 49 8f d2 68 7e ed dc ce cf d3 51 bd 8d d2
  //   3 49 ad c6 c7 8b e1 b 88 88 d2 1f 48 d2 50 a8 d3 4 c6 8a e1 b2 e0 80 d4
endmodule

module _16_16_matrix (
  input  [7:0] Lo_byte,
  input  Lo_byte_on,
  input  [7:0] Hi_byte,
  input  Hi_byte_On,
  input  [7:0] Selector,
  input  Selection_On,
  input  Bus_0
);

  wire clk, demultiplexer_1_out0, demultiplexer_1_out1, demultiplexer_1_out2, demultiplexer_1_out3,
       demultiplexer_1_out4, demultiplexer_1_out5, demultiplexer_1_out6, demultiplexer_1_out7,
       demultiplexer_1_out8, demultiplexer_1_out9, demultiplexer_1_out10, demultiplexer_1_out11,
       demultiplexer_1_out12, demultiplexer_1_out13, demultiplexer_1_out14, demultiplexer_1_out15, undriven,
       undriven_2;
  wire [7:0] register_1_q, register_2_q, register_3_q;
  wire [15:0] register_4_q, register_5_q, register_6_q, register_7_q, register_8_q, register_10_q,
       register_11_q, register_12_q, register_13_q, register_14_q, register_15_q, register_16_q,
       register_17_q, register_18_q, register_19_q, undriven_3;

  Clock clock_1 (.out(clk));
  Register register_1 (.D(Lo_byte), .en(Lo_byte_on), .Q(register_1_q), .clk(undriven));  // open: clr
  Register register_2 (.D(Hi_byte), .en(Hi_byte_On), .Q(register_2_q), .clk(clk));  // open: clr
  Register #(.trigger("high")) register_3 (.D(Selector), .en(Selection_On), .Q(register_3_q), .clk(clk));  // open: clr
  // Probe on register_3_q
  Demultiplexer #(.select(4), .disabled(0)) demultiplexer_1 (
    .out0(demultiplexer_1_out0), .out1(demultiplexer_1_out1), .out2(demultiplexer_1_out2),
    .out3(demultiplexer_1_out3), .out4(demultiplexer_1_out4), .out5(demultiplexer_1_out5),
    .out6(demultiplexer_1_out6), .out7(demultiplexer_1_out7), .out8(demultiplexer_1_out8),
    .out9(demultiplexer_1_out9), .out10(demultiplexer_1_out10), .out11(demultiplexer_1_out11),
    .out12(demultiplexer_1_out12), .out13(demultiplexer_1_out13), .out14(demultiplexer_1_out14),
    .out15(demultiplexer_1_out15), .in(Selection_On), .sel(register_3_q[3:0]), .en(Selection_On));
  Register #(.width(16)) register_4 (
    .D({register_2_q, register_1_q}), .en(demultiplexer_1_out0), .Q(register_4_q), .clk(clk));  // open: clr
  Register #(.width(16)) register_5 (
    .D({register_2_q, register_1_q}), .en(demultiplexer_1_out1), .Q(register_5_q), .clk(clk));  // open: clr
  Register #(.width(16)) register_6 (
    .D({register_2_q, register_1_q}), .en(demultiplexer_1_out2), .Q(register_6_q), .clk(clk));  // open: clr
  Register #(.width(16)) register_7 (
    .D({register_2_q, register_1_q}), .en(demultiplexer_1_out3), .Q(register_7_q), .clk(clk));  // open: clr
  Register #(.width(16)) register_8 (
    .D({register_2_q, register_1_q}), .en(demultiplexer_1_out4), .Q(register_8_q), .clk(clk), .clr(undriven_2));
  Register #(.width(16)) register_9 (
    .D({register_2_q, register_1_q}), .en(demultiplexer_1_out4), .Q(register_8_q), .clk(clk), .clr(undriven_2));
  Register #(.width(16)) register_10 (
    .D({register_2_q, register_1_q}), .en(demultiplexer_1_out5), .Q(register_10_q), .clk(clk));  // open: clr
  Register #(.width(16)) register_11 (
    .D({register_2_q, register_1_q}), .en(demultiplexer_1_out7), .Q(register_11_q), .clk(clk));  // open: clr
  Register #(.width(16)) register_12 (
    .D({register_2_q, register_1_q}), .en(demultiplexer_1_out8), .Q(register_12_q), .clk(clk));  // open: clr
  Register #(.width(16)) register_13 (
    .D({register_2_q, register_1_q}), .en(demultiplexer_1_out9), .Q(register_13_q), .clk(clk));  // open: clr
  Register #(.width(16)) register_14 (
    .D({register_2_q, register_1_q}), .en(demultiplexer_1_out10), .Q(register_14_q), .clk(clk));  // open: clr
  Register #(.width(16)) register_15 (
    .D({register_2_q, register_1_q}), .en(demultiplexer_1_out11), .Q(register_15_q), .clk(clk));  // open: clr
  Register #(.width(16)) register_16 (
    .D({register_2_q, register_1_q}), .en(demultiplexer_1_out12), .Q(register_16_q), .clk(clk));  // open: clr
  Register #(.width(16)) register_17 (
    .D({register_2_q, register_1_q}), .en(demultiplexer_1_out13), .Q(register_17_q), .clk(clk));  // open: clr
  Register #(.width(16)) register_18 (
    .D({register_2_q, register_1_q}), .en(demultiplexer_1_out14), .Q(register_18_q), .clk(clk));  // open: clr
  Register #(.width(16)) register_19 (
    .D({register_2_q, register_1_q}), .en(demultiplexer_1_out15), .Q(register_19_q), .clk(clk));  // open: clr
  DotMatrix #(.inputtype("row"), .matrixcols(16), .matrixrows(16)) dotmatrix_1 (
    .row0(register_4_q), .row1(register_5_q), .row2(register_6_q), .row3(register_7_q), .row4(register_8_q),
    .row5(register_10_q), .row6(undriven_3), .row7(register_11_q), .row8(register_12_q),
    .row9(register_13_q), .row10(register_14_q), .row11(register_15_q), .row12(register_16_q),
    .row13(register_17_q), .row14(register_18_q), .row15(register_19_q));
  DotMatrix #(.inputtype("row"), .matrixcols(16), .matrixrows(16)) dotmatrix_2 (
    .row0(register_4_q), .row1(register_5_q), .row2(register_6_q), .row3(register_7_q), .row4(register_8_q),
    .row5(register_10_q), .row6(undriven_3), .row7(register_11_q), .row8(register_12_q),
    .row9(register_13_q), .row10(register_14_q), .row11(register_15_q), .row12(register_16_q),
    .row13(register_17_q), .row14(register_18_q), .row15(register_19_q));
endmodule

module _16_16_demonstration (
  input  Full_On,
  input  Selection_On,
  input  Bus_0
);

  wire clk, demultiplexer_1_out0, demultiplexer_1_out1, demultiplexer_1_out2, demultiplexer_1_out3,
       demultiplexer_1_out4, demultiplexer_1_out5, demultiplexer_1_out6, demultiplexer_1_out7,
       demultiplexer_1_out8, demultiplexer_1_out9, demultiplexer_1_out10, demultiplexer_1_out11,
       demultiplexer_1_out12, demultiplexer_1_out13, demultiplexer_1_out14, demultiplexer_1_out15, rst,
       undriven;
  wire [3:0] random_1_out;
  wire [15:0] random_2_out, register_1_q, register_2_q, register_3_q, register_4_q, register_5_q,
       register_6_q, register_7_q, register_8_q, register_9_q, register_10_q, register_11_q, register_12_q,
       register_13_q, register_14_q, register_15_q, register_16_q;

  Clock clock_1 (.out(clk));
  Button Reset (.out(rst));
  Demultiplexer #(.select(4), .disabled(0)) demultiplexer_1 (
    .out0(demultiplexer_1_out0), .out1(demultiplexer_1_out1), .out2(demultiplexer_1_out2),
    .out3(demultiplexer_1_out3), .out4(demultiplexer_1_out4), .out5(demultiplexer_1_out5),
    .out6(demultiplexer_1_out6), .out7(demultiplexer_1_out7), .out8(demultiplexer_1_out8),
    .out9(demultiplexer_1_out9), .out10(demultiplexer_1_out10), .out11(demultiplexer_1_out11),
    .out12(demultiplexer_1_out12), .out13(demultiplexer_1_out13), .out14(demultiplexer_1_out14),
    .out15(demultiplexer_1_out15), .in(Selection_On), .sel(random_1_out), .en(Selection_On));
  Random #(.width(4)) random_1 (.clk(clk), .next(Full_On), .out(random_1_out), .clr(rst));
  Random #(.width(16), .seed(5)) random_2 (.clk(clk), .next(Full_On), .out(random_2_out), .clr(rst));
  Register #(.width(16)) register_1 (
    .D(random_2_out), .en(demultiplexer_1_out0), .Q(register_1_q), .clk(clk), .clr(rst));
  Register #(.width(16)) register_2 (
    .D(random_2_out), .en(demultiplexer_1_out1), .Q(register_2_q), .clk(Full_On), .clr(rst));
  Register #(.width(16)) register_3 (
    .D(random_2_out), .en(demultiplexer_1_out2), .Q(register_3_q), .clk(clk), .clr(rst));
  Register #(.width(16)) register_4 (
    .D(random_2_out), .en(demultiplexer_1_out3), .Q(register_4_q), .clk(clk), .clr(rst));
  Register #(.width(16)) register_5 (
    .D(random_2_out), .en(demultiplexer_1_out4), .Q(register_5_q), .clk(clk), .clr(rst));
  Register #(.width(16)) register_6 (
    .D(random_2_out), .en(demultiplexer_1_out5), .Q(register_6_q), .clk(clk), .clr(rst));
  Register #(.width(16)) register_7 (
    .D(random_2_out), .en(demultiplexer_1_out6), .Q(register_7_q), .clk(clk), .clr(rst));
  Register #(.width(16)) register_8 (
    .D(random_2_out), .en(demultiplexer_1_out7), .Q(register_8_q), .clk(clk), .clr(rst));
  Register #(.width(16)) register_9 (
    .D(random_2_out), .en(demultiplexer_1_out8), .Q(register_9_q), .clk(clk), .clr(rst));
  Register #(.width(16)) register_10 (
    .D(random_2_out), .en(demultiplexer_1_out9), .Q(register_10_q), .clk(clk), .clr(rst));
  Register #(.width(16)) register_11 (
    .D(random_2_out), .en(demultiplexer_1_out10), .Q(register_11_q), .clk(clk), .clr(rst));
  Register #(.width(16)) register_12 (
    .D(random_2_out), .en(demultiplexer_1_out11), .Q(register_12_q), .clk(undriven), .clr(rst));
  Register #(.width(16)) register_13 (
    .D(random_2_out), .en(demultiplexer_1_out12), .Q(register_13_q), .clk(clk), .clr(rst));
  Register #(.width(16)) register_14 (
    .D(random_2_out), .en(demultiplexer_1_out13), .Q(register_14_q), .clk(clk), .clr(rst));
  Register #(.width(16)) register_15 (
    .D(random_2_out), .en(demultiplexer_1_out14), .Q(register_15_q), .clk(clk), .clr(rst));
  Register #(.width(16)) register_16 (
    .D(random_2_out), .en(demultiplexer_1_out15), .Q(register_16_q), .clk(clk), .clr(rst));
  DotMatrix #(.inputtype("row"), .matrixcols(16), .matrixrows(16)) dotmatrix_1 (
    .row0(register_1_q), .row1(register_2_q), .row2(register_3_q), .row3(register_4_q), .row4(register_5_q),
    .row5(register_6_q), .row6(register_7_q), .row7(register_8_q), .row8(register_9_q), .row9(register_10_q),
    .row10(register_11_q), .row11(register_12_q), .row12(register_13_q), .row13(register_14_q),
    .row14(register_15_q), .row15(register_16_q));

  // Other names for the same wires on the sheet: on = Full_On
endmodule

module _32_32_matrix (
  input  [7:0] _0_byte,
  input  _0_byte_on,
  input  [7:0] _1_byte,
  input  _1_byte_On,
  input  [7:0] _2_byte,
  input  _2_byte_on,
  input  [7:0] _3_byte,
  input  _3_byte_On,
  input  [7:0] Selector,
  input  Selection_On,
  input  Bus_0
);

  wire clk, demultiplexer_1_out0, demultiplexer_1_out1, demultiplexer_1_out2, demultiplexer_1_out3,
       demultiplexer_1_out4, demultiplexer_1_out5, demultiplexer_1_out6, demultiplexer_1_out7,
       demultiplexer_1_out8, demultiplexer_1_out9, demultiplexer_1_out10, demultiplexer_1_out11,
       demultiplexer_1_out12, demultiplexer_1_out13, demultiplexer_1_out14, demultiplexer_1_out15,
       demultiplexer_1_out16, demultiplexer_1_out17, demultiplexer_1_out18, demultiplexer_1_out19,
       demultiplexer_1_out20, demultiplexer_1_out21, demultiplexer_1_out22, demultiplexer_1_out23,
       demultiplexer_1_out24, demultiplexer_1_out25, demultiplexer_1_out26, demultiplexer_1_out27,
       demultiplexer_1_out28, demultiplexer_1_out29, demultiplexer_1_out30, demultiplexer_1_out31, undriven;
  wire [7:0] register_1_q, register_2_q, register_3_q, register_4_q, register_5_q;
  wire [31:0] register_6_q, register_7_q, register_8_q, register_9_q, register_10_q, register_11_q,
       register_12_q, register_13_q, register_14_q, register_15_q, register_16_q, register_17_q,
       register_18_q, register_19_q, register_20_q, register_21_q, register_22_q, register_23_q,
       register_24_q, register_25_q, register_27_q, register_28_q, register_29_q, register_30_q,
       register_31_q, register_32_q, register_33_q, register_34_q, register_35_q, register_36_q,
       register_37_q, undriven_2;

  Clock clock_1 (.out(clk));
  Register register_1 (.D(_0_byte), .en(_0_byte_on), .Q(register_1_q), .clk(clk));  // open: clr
  Register register_2 (.D(_1_byte), .en(_1_byte_On), .Q(register_2_q), .clk(clk));  // open: clr
  Register register_3 (.D(_2_byte), .en(_2_byte_on), .Q(register_3_q), .clk(clk));  // open: clr
  Register register_4 (.D(_3_byte), .en(_3_byte_On), .Q(register_4_q), .clk(clk));  // open: clr
  Register #(.trigger("high")) register_5 (.D(Selector), .en(Selection_On), .Q(register_5_q), .clk(clk));  // open: clr
  // Probe on register_5_q
  Demultiplexer #(.select(5), .disabled(0)) demultiplexer_1 (
    .out0(demultiplexer_1_out0), .out1(demultiplexer_1_out1), .out2(demultiplexer_1_out2),
    .out3(demultiplexer_1_out3), .out4(demultiplexer_1_out4), .out5(demultiplexer_1_out5),
    .out6(demultiplexer_1_out6), .out7(demultiplexer_1_out7), .out8(demultiplexer_1_out8),
    .out9(demultiplexer_1_out9), .out10(demultiplexer_1_out10), .out11(demultiplexer_1_out11),
    .out12(demultiplexer_1_out12), .out13(demultiplexer_1_out13), .out14(demultiplexer_1_out14),
    .out15(demultiplexer_1_out15), .out16(demultiplexer_1_out16), .out17(demultiplexer_1_out17),
    .out18(demultiplexer_1_out18), .out19(demultiplexer_1_out19), .out20(demultiplexer_1_out20),
    .out21(demultiplexer_1_out21), .out22(demultiplexer_1_out22), .out23(demultiplexer_1_out23),
    .out24(demultiplexer_1_out24), .out25(demultiplexer_1_out25), .out26(demultiplexer_1_out26),
    .out27(demultiplexer_1_out27), .out28(demultiplexer_1_out28), .out29(demultiplexer_1_out29),
    .out30(demultiplexer_1_out30), .out31(demultiplexer_1_out31), .in(Selection_On), .sel(register_5_q[4:0]));  // open: en
  Register #(.width(32)) register_6 (
    .D({register_4_q, register_3_q, register_2_q, register_1_q}), .en(demultiplexer_1_out0),
    .Q(register_6_q), .clk(clk));  // open: clr
  Register #(.width(32)) register_7 (
    .D({register_4_q, register_3_q, register_2_q, register_1_q}), .en(demultiplexer_1_out1),
    .Q(register_7_q), .clk(clk));  // open: clr
  Register #(.width(32)) register_8 (
    .D({register_4_q, register_3_q, register_2_q, register_1_q}), .en(demultiplexer_1_out2),
    .Q(register_8_q), .clk(clk));  // open: clr
  Register #(.width(32)) register_9 (
    .D({register_4_q, register_3_q, register_2_q, register_1_q}), .en(demultiplexer_1_out3),
    .Q(register_9_q), .clk(clk));  // open: clr
  Register #(.width(32)) register_10 (
    .D({register_4_q, register_3_q, register_2_q, register_1_q}), .en(demultiplexer_1_out4),
    .Q(register_10_q), .clk(clk));  // open: clr
  Register #(.width(32)) register_11 (
    .D({register_4_q, register_3_q, register_2_q, register_1_q}), .en(demultiplexer_1_out5),
    .Q(register_11_q), .clk(clk));  // open: clr
  Register #(.width(32)) register_12 (
    .D({register_4_q, register_3_q, register_2_q, register_1_q}), .en(demultiplexer_1_out6),
    .Q(register_12_q), .clk(clk));  // open: clr
  Register #(.width(32)) register_13 (
    .D({register_4_q, register_3_q, register_2_q, register_1_q}), .en(demultiplexer_1_out7),
    .Q(register_13_q), .clk(clk));  // open: clr
  Register #(.width(32)) register_14 (
    .D({register_4_q, register_3_q, register_2_q, register_1_q}), .en(demultiplexer_1_out8),
    .Q(register_14_q), .clk(clk));  // open: clr
  Register #(.width(32)) register_15 (
    .D({register_4_q, register_3_q, register_2_q, register_1_q}), .en(demultiplexer_1_out9),
    .Q(register_15_q), .clk(clk));  // open: clr
  Register #(.width(32)) register_16 (
    .D({register_4_q, register_3_q, register_2_q, register_1_q}), .en(demultiplexer_1_out10),
    .Q(register_16_q), .clk(clk));  // open: clr
  Register #(.width(32)) register_17 (
    .D({register_4_q, register_3_q, register_2_q, register_1_q}), .en(demultiplexer_1_out12),
    .Q(register_17_q), .clk(clk));  // open: clr
  Register #(.width(32)) register_18 (
    .D({register_4_q, register_3_q, register_2_q, register_1_q}), .en(demultiplexer_1_out13),
    .Q(register_18_q), .clk(clk));  // open: clr
  Register #(.width(32)) register_19 (
    .D({register_4_q, register_3_q, register_2_q, register_1_q}), .en(demultiplexer_1_out14),
    .Q(register_19_q), .clk(clk));  // open: clr
  Register #(.width(32)) register_20 (
    .D({register_4_q, register_3_q, register_2_q, register_1_q}), .en(demultiplexer_1_out15),
    .Q(register_20_q), .clk(clk));  // open: clr
  Register #(.width(32)) register_21 (
    .D({register_4_q, register_3_q, register_2_q, register_1_q}), .en(demultiplexer_1_out16),
    .Q(register_21_q), .clk(clk));  // open: clr
  Register #(.width(32)) register_22 (
    .D({register_4_q, register_3_q, register_2_q, register_1_q}), .en(demultiplexer_1_out17),
    .Q(register_22_q), .clk(clk));  // open: clr
  Register #(.width(32)) register_23 (
    .D({register_4_q, register_3_q, register_2_q, register_1_q}), .en(demultiplexer_1_out18),
    .Q(register_23_q), .clk(clk));  // open: clr
  Register #(.width(32)) register_24 (
    .D({register_4_q, register_3_q, register_2_q, register_1_q}), .en(demultiplexer_1_out19),
    .Q(register_24_q), .clk(clk));  // open: clr
  Register #(.width(32)) register_25 (
    .D({register_4_q, register_3_q, register_2_q, register_1_q}), .en(demultiplexer_1_out20),
    .Q(register_25_q), .clk(clk), .clr(undriven));
  Register #(.width(32)) register_26 (
    .D({register_4_q, register_3_q, register_2_q, register_1_q}), .en(demultiplexer_1_out20),
    .Q(register_25_q), .clk(clk), .clr(undriven));
  Register #(.width(32)) register_27 (
    .D({register_4_q, register_3_q, register_2_q, register_1_q}), .en(demultiplexer_1_out21),
    .Q(register_27_q), .clk(clk));  // open: clr
  Register #(.width(32)) register_28 (
    .D({register_4_q, register_3_q, register_2_q, register_1_q}), .en(demultiplexer_1_out22),
    .Q(register_28_q), .clk(clk));  // open: clr
  Register #(.width(32)) register_29 (
    .D({register_4_q, register_3_q, register_2_q, register_1_q}), .en(demultiplexer_1_out23),
    .Q(register_29_q), .clk(clk));  // open: clr
  Register #(.width(32)) register_30 (
    .D({register_4_q, register_3_q, register_2_q, register_1_q}), .en(demultiplexer_1_out24),
    .Q(register_30_q), .clk(clk));  // open: clr
  Register #(.width(32)) register_31 (
    .D({register_4_q, register_3_q, register_2_q, register_1_q}), .en(demultiplexer_1_out25),
    .Q(register_31_q), .clk(clk));  // open: clr
  Register #(.width(32)) register_32 (
    .D({register_4_q, register_3_q, register_2_q, register_1_q}), .en(demultiplexer_1_out26),
    .Q(register_32_q), .clk(clk));  // open: clr
  Register #(.width(32)) register_33 (
    .D({register_4_q, register_3_q, register_2_q, register_1_q}), .en(demultiplexer_1_out27),
    .Q(register_33_q), .clk(clk));  // open: clr
  Register #(.width(32)) register_34 (
    .D({register_4_q, register_3_q, register_2_q, register_1_q}), .en(demultiplexer_1_out28),
    .Q(register_34_q), .clk(clk));  // open: clr
  Register #(.width(32)) register_35 (
    .D({register_4_q, register_3_q, register_2_q, register_1_q}), .en(demultiplexer_1_out29),
    .Q(register_35_q), .clk(clk));  // open: clr
  Register #(.width(32)) register_36 (
    .D({register_4_q, register_3_q, register_2_q, register_1_q}), .en(demultiplexer_1_out30),
    .Q(register_36_q), .clk(clk));  // open: clr
  Register #(.width(32)) register_37 (
    .D({register_4_q, register_3_q, register_2_q, register_1_q}), .en(demultiplexer_1_out31),
    .Q(register_37_q), .clk(clk));  // open: clr
  DotMatrix #(.inputtype("row"), .matrixcols(32), .matrixrows(32)) dotmatrix_1 (
    .row0(register_6_q), .row1(register_7_q), .row2(register_8_q), .row3(register_9_q), .row4(register_10_q),
    .row5(register_11_q), .row6(register_12_q), .row7(register_13_q), .row8(register_14_q),
    .row9(register_15_q), .row10(register_16_q), .row11(undriven_2), .row12(register_17_q),
    .row13(register_18_q), .row14(register_19_q), .row15(register_20_q), .row16(register_21_q),
    .row17(register_22_q), .row18(register_23_q), .row19(register_24_q), .row20(register_25_q),
    .row21(register_27_q), .row22(register_28_q), .row23(register_29_q), .row24(register_30_q),
    .row25(register_31_q), .row26(register_32_q), .row27(register_33_q), .row28(register_34_q),
    .row29(register_35_q), .row30(register_36_q), .row31(register_37_q));
endmodule

module _32_32_demo (
  input  Full_On,
  input  Selection_On,
  input  [4:0] Y,
  input  [4:0] X,
  output [31:0] out_5,
  output [7:0] out_6,
  output out_7
);

  wire n32_32_buffer_1_p40;
  wire [7:0] counter_1_q;
  wire [31:0] n32_32_buffer_1_p7, n32_32_buffer_1_p8, n32_32_buffer_1_p9, n32_32_buffer_1_p10,
       n32_32_buffer_1_p11, n32_32_buffer_1_p12, n32_32_buffer_1_p13, n32_32_buffer_1_p14,
       n32_32_buffer_1_p15, n32_32_buffer_1_p16, n32_32_buffer_1_p17, n32_32_buffer_1_p18,
       n32_32_buffer_1_p19, n32_32_buffer_1_p20, n32_32_buffer_1_p21, n32_32_buffer_1_p22,
       n32_32_buffer_1_p23, n32_32_buffer_1_p24, n32_32_buffer_1_p25, n32_32_buffer_1_p26,
       n32_32_buffer_1_p27, n32_32_buffer_1_p28, n32_32_buffer_1_p29, n32_32_buffer_1_p30,
       n32_32_buffer_1_p31, n32_32_buffer_1_p32, n32_32_buffer_1_p33, n32_32_buffer_1_p34,
       n32_32_buffer_1_p35, n32_32_buffer_1_p36, n32_32_buffer_1_p37, n32_32_buffer_1_p38, random_1_out;

  Clock clock_1 (.out(Full_On));
  Random #(.width(32), .seed(10)) random_1 (.clk(Full_On), .next(Full_On), .out(random_1_out));  // open: clr
  Counter #(.max('h1f)) counter_1 (.count(Full_On), .Q(counter_1_q), .clk(Full_On));  // open: load, D, carry, clr
  // _32_32_buffer 32_32_buffer_1: pin names not known; wires that end beside it: Full_On, random_1_out, counter_1_q, Selection_On, Y, X, n32_32_buffer_1_p7, n32_32_buffer_1_p8, n32_32_buffer_1_p9, n32_32_buffer_1_p10, n32_32_buffer_1_p11, n32_32_buffer_1_p12, n32_32_buffer_1_p13, n32_32_buffer_1_p14, n32_32_buffer_1_p15, n32_32_buffer_1_p16, n32_32_buffer_1_p17, n32_32_buffer_1_p18, n32_32_buffer_1_p19, n32_32_buffer_1_p20, n32_32_buffer_1_p21, n32_32_buffer_1_p22, n32_32_buffer_1_p23, n32_32_buffer_1_p24, n32_32_buffer_1_p25, n32_32_buffer_1_p26, n32_32_buffer_1_p27, n32_32_buffer_1_p28, n32_32_buffer_1_p29, n32_32_buffer_1_p30, n32_32_buffer_1_p31, n32_32_buffer_1_p32, n32_32_buffer_1_p33, n32_32_buffer_1_p34, n32_32_buffer_1_p35, n32_32_buffer_1_p36, n32_32_buffer_1_p37, n32_32_buffer_1_p38, out_5, n32_32_buffer_1_p40, out_6, out_7
  // _32_32_buffer 32_32_buffer_2: pin names not known; wires that end beside it: Full_On, random_1_out, counter_1_q, Selection_On, Y, X, n32_32_buffer_1_p7, n32_32_buffer_1_p8, n32_32_buffer_1_p9, n32_32_buffer_1_p10, n32_32_buffer_1_p11, n32_32_buffer_1_p12, n32_32_buffer_1_p13, n32_32_buffer_1_p14, n32_32_buffer_1_p15, n32_32_buffer_1_p16, n32_32_buffer_1_p17, n32_32_buffer_1_p18, n32_32_buffer_1_p19, n32_32_buffer_1_p20, n32_32_buffer_1_p21, n32_32_buffer_1_p22, n32_32_buffer_1_p23, n32_32_buffer_1_p24, n32_32_buffer_1_p25, n32_32_buffer_1_p26, n32_32_buffer_1_p27, n32_32_buffer_1_p28, n32_32_buffer_1_p29, n32_32_buffer_1_p30, n32_32_buffer_1_p31, n32_32_buffer_1_p32, n32_32_buffer_1_p33, n32_32_buffer_1_p34, n32_32_buffer_1_p35, n32_32_buffer_1_p36, n32_32_buffer_1_p37, n32_32_buffer_1_p38, out_5, n32_32_buffer_1_p40, out_6, out_7
  // Probe on Y
  // Probe on Y
  // Probe on X
  // Probe on X
  DotMatrix #(.inputtype("row"), .matrixcols(32), .matrixrows(32)) dotmatrix_1 (
    .row0(n32_32_buffer_1_p7), .row1(n32_32_buffer_1_p8), .row2(n32_32_buffer_1_p9),
    .row3(n32_32_buffer_1_p10), .row4(n32_32_buffer_1_p11), .row5(n32_32_buffer_1_p12),
    .row6(n32_32_buffer_1_p13), .row7(n32_32_buffer_1_p14), .row8(n32_32_buffer_1_p15),
    .row9(n32_32_buffer_1_p16), .row10(n32_32_buffer_1_p17), .row11(n32_32_buffer_1_p18),
    .row12(n32_32_buffer_1_p19), .row13(n32_32_buffer_1_p20), .row14(n32_32_buffer_1_p21),
    .row15(n32_32_buffer_1_p22), .row16(n32_32_buffer_1_p23), .row17(n32_32_buffer_1_p24),
    .row18(n32_32_buffer_1_p25), .row19(n32_32_buffer_1_p26), .row20(n32_32_buffer_1_p27),
    .row21(n32_32_buffer_1_p28), .row22(n32_32_buffer_1_p29), .row23(n32_32_buffer_1_p30),
    .row24(n32_32_buffer_1_p31), .row25(n32_32_buffer_1_p32), .row26(n32_32_buffer_1_p33),
    .row27(n32_32_buffer_1_p34), .row28(n32_32_buffer_1_p35), .row29(n32_32_buffer_1_p36),
    .row30(n32_32_buffer_1_p37), .row31(n32_32_buffer_1_p38));

  // Other names for the same wires on the sheet: clk = Full_On; on = Full_On
endmodule

module _32_32_buffer (
  input  [4:0] Row_selector,
  input  Write_row,
  input  clock,
  output [31:0] Row_0,
  output [31:0] Row_1,
  output [31:0] Row_2,
  output [31:0] Row_2_2,
  output [31:0] Row_3,
  output [31:0] Row_4,
  output [31:0] Row_5,
  output [31:0] Row_6,
  output [31:0] Row_6_2,
  output [31:0] Row_7,
  output [31:0] Row_8,
  output [31:0] Row_8_2,
  output [31:0] Row_4_2,
  output [31:0] Row_10,
  output [31:0] Row_11,
  output [31:0] Row_12,
  output [31:0] Row_13,
  output [31:0] Row_15,
  output [31:0] Row_15_2,
  output [31:0] Selected_row_output,
  output [31:0] Row_29,
  output [31:0] Row_17,
  output [31:0] Row_18,
  output [31:0] Row_19,
  output [31:0] Row_20,
  output [31:0] Row_21,
  output [31:0] Row_22,
  output [31:0] Row_23,
  output [31:0] Row_24,
  output [31:0] Row_25,
  output [31:0] Row_26,
  output [31:0] Row_28,
  output [31:0] Row_29_2,
  output [31:0] Row_30,
  output [31:0] Row_31
);

  wire decoder_1_out0, decoder_1_out1, decoder_1_out2, decoder_1_out3, decoder_1_out4, decoder_1_out5,
       decoder_1_out6, decoder_1_out7, decoder_1_out8, decoder_1_out9, decoder_1_out10, decoder_1_out11,
       decoder_1_out12, decoder_1_out13, decoder_1_out14, decoder_1_out15, decoder_1_out16, decoder_1_out17,
       decoder_1_out18, decoder_1_out19, decoder_1_out20, decoder_1_out21, decoder_1_out22, decoder_1_out23,
       decoder_1_out24, decoder_1_out25, decoder_1_out26, decoder_1_out27, decoder_1_out28, decoder_1_out29,
       decoder_1_out30, decoder_1_out31, undriven_2, undriven_3;
  wire [4:0] undriven_4;
  wire [31:0] register_26_q, undriven;

  Decoder #(.select(5), .disabled(0)) decoder_1 (
    .out0(decoder_1_out0), .out1(decoder_1_out1), .out2(decoder_1_out2), .out3(decoder_1_out3),
    .out4(decoder_1_out4), .out5(decoder_1_out5), .out6(decoder_1_out6), .out7(decoder_1_out7),
    .out8(decoder_1_out8), .out9(decoder_1_out9), .out10(decoder_1_out10), .out11(decoder_1_out11),
    .out12(decoder_1_out12), .out13(decoder_1_out13), .out14(decoder_1_out14), .out15(decoder_1_out15),
    .out16(decoder_1_out16), .out17(decoder_1_out17), .out18(decoder_1_out18), .out19(decoder_1_out19),
    .out20(decoder_1_out20), .out21(decoder_1_out21), .out22(decoder_1_out22), .out23(decoder_1_out23),
    .out24(decoder_1_out24), .out25(decoder_1_out25), .out26(decoder_1_out26), .out27(decoder_1_out27),
    .out28(decoder_1_out28), .out29(decoder_1_out29), .out30(decoder_1_out30), .out31(decoder_1_out31),
    .sel(Row_selector), .en(Write_row));
  Register #(.width(32)) register_1 (.D(undriven), .en(undriven_2), .Q(Row_0), .clk(decoder_1_out0), .clr(undriven_3));
  Register #(.width(32)) register_2 (.D(undriven), .en(undriven_2), .Q(Row_0), .clk(decoder_1_out0), .clr(undriven_3));
  Register #(.width(32)) u_Row_28 (.D(undriven), .Q(Row_1), .clk(decoder_1_out1));  // open: en, clr
  Register #(.width(32)) register_3 (.D(undriven), .Q(Row_2), .clk(decoder_1_out2));  // open: en, clr
  Register #(.width(32)) register_4 (.D(undriven), .Q(Row_3), .clk(decoder_1_out3));  // open: en, clr
  Register #(.width(32), .tristate("false")) Input_row (
    .D(undriven), .Q(Row_4), .clk(decoder_1_out4));  // open: en, clr
  Register #(.width(32)) register_5 (.D(undriven), .Q(Row_5), .clk(decoder_1_out5));  // open: en, clr
  Register #(.width(32)) register_6 (.D(undriven), .Q(Row_6), .clk(decoder_1_out6));  // open: en, clr
  Register #(.width(32)) register_7 (.D(undriven), .Q(Row_7), .clk(decoder_1_out7));  // open: en, clr
  Register #(.width(32)) Row_27 (.D(undriven), .Q(Row_8), .clk(decoder_1_out8));  // open: en, clr
  Register #(.width(32)) register_8 (.D(undriven), .Q(Row_4_2), .clk(decoder_1_out9));  // open: en, clr
  Register #(.width(32)) register_9 (.D(undriven), .Q(Row_10), .clk(decoder_1_out10));  // open: en, clr
  Register #(.width(32)) register_10 (.D(undriven), .Q(Row_11), .clk(decoder_1_out11));  // open: en, clr
  Register #(.width(32)) register_11 (.D(undriven), .Q(Row_12), .clk(decoder_1_out12));  // open: en, clr
  Register #(.width(32)) register_12 (.D(undriven), .Q(Row_13), .clk(decoder_1_out13));  // open: en, clr
  Register #(.width(32)) register_13 (.D(undriven), .Q(Row_15), .clk(decoder_1_out14));  // open: en, clr
  Register #(.width(32)) register_14 (.D(undriven), .Q(Row_15_2), .clk(decoder_1_out15));  // open: en, clr
  Register #(.width(32)) register_15 (.D(undriven), .Q(Row_29), .clk(decoder_1_out16));  // open: en, clr
  Register #(.width(32)) register_16 (.D(undriven), .Q(Row_17), .clk(decoder_1_out17));  // open: en, clr
  Register #(.width(32)) register_17 (.D(undriven), .Q(Row_18), .clk(decoder_1_out18));  // open: en, clr
  Register #(.width(32)) register_18 (.D(undriven), .Q(Row_19), .clk(decoder_1_out19));  // open: en, clr
  Register #(.width(32)) register_19 (.D(undriven), .Q(Row_20), .clk(decoder_1_out20));  // open: en, clr
  Register #(.width(32)) register_20 (.D(undriven), .Q(Row_21), .clk(decoder_1_out21));  // open: en, clr
  Register #(.width(32)) register_21 (.D(undriven), .Q(Row_22), .clk(decoder_1_out22));  // open: en, clr
  Register #(.width(32)) register_22 (.D(undriven), .Q(Row_23), .clk(decoder_1_out23));  // open: en, clr
  Register #(.width(32)) register_23 (.D(undriven), .Q(Row_24), .clk(decoder_1_out24));  // open: en, clr
  Register #(.width(32)) register_24 (.D(undriven), .Q(Row_25), .clk(decoder_1_out25));  // open: en, clr
  Register #(.width(32)) register_25 (.D(undriven), .Q(Row_26), .clk(decoder_1_out26));  // open: en, clr
  Register #(.width(32)) register_26 (.D(undriven), .Q(register_26_q), .clk(decoder_1_out27));  // open: en, clr
  Register #(.width(32)) register_27 (.D(undriven), .Q(Row_28), .clk(decoder_1_out28));  // open: en, clr
  Register #(.width(32)) register_28 (.D(undriven), .Q(Row_29_2), .clk(decoder_1_out29));  // open: en, clr
  Register #(.width(32)) register_29 (.D(undriven), .Q(Row_31), .clk(decoder_1_out31));  // open: en, clr
  Multiplexer #(.select(5), .width(32), .enable("false")) multiplexer_1 (
    .in0(Row_0), .in1(Row_1), .in2(Row_2), .in3(Row_3), .in4(Row_4), .in5(Row_5), .in6(Row_6), .in7(Row_7),
    .in8(Row_8), .in9(Row_4_2), .in10(Row_10), .in11(Row_11), .in12(Row_12), .in13(Row_13), .in14(Row_15),
    .in15(Row_15_2), .in16(Row_29), .in17(Row_17), .in18(Row_18), .in19(Row_19), .in20(Row_20),
    .in21(Row_21), .in22(Row_22), .in23(Row_23), .in24(Row_24), .in25(Row_25), .in26(Row_26),
    .in27(register_26_q), .in28(Row_28), .in29(Row_29_2), .in30(Row_30), .in31(Row_31),
    .out(Selected_row_output), .sel(undriven_4));
  // Probe on undriven_4

  assign Row_2_2 = Row_2;
  assign Row_6_2 = Row_6;
  assign Row_8_2 = Row_8;
endmodule

module Keyboard_controller (
  input  [6:0] ASCII_code,
  output [4:0] X,
  output Switch
);

  wire _0x_y, _0x_y_t, minus_x0y, minus_x_y, minus_x_y_t, or_1_out, or_2_out, or_3_out, or_4_out, or_5_out,
       or_6_out, plus_x0y, plus_x_y, plus_x_y_t;
  wire [4:0] counter_1_q;

  Comparator #(.width(7)) comparator_1 (.a(ASCII_code), .b(7'b0110111), .eq(minus_x_y_t));  // open: gt, lt
  Comparator #(.width(7)) comparator_2 (.a(ASCII_code), .b(7'b0110100), .eq(minus_x0y));  // open: gt, lt
  Comparator #(.width(7)) comparator_3 (.a(ASCII_code), .b(7'b0110001), .eq(minus_x_y));  // open: gt, lt
  Comparator #(.width(7)) comparator_4 (.a(ASCII_code), .b(7'b0000001), .eq(_0x_y_t));  // open: gt, lt
  Comparator #(.width(7)) comparator_5 (.a(ASCII_code), .b(7'b0110101), .eq(Switch));  // open: gt, lt
  Comparator #(.width(7)) comparator_6 (.a(ASCII_code), .b(7'b0110010), .eq(_0x_y));  // open: gt, lt
  Comparator #(.width(7), .value('h38)) comparator_7 (.a(ASCII_code), .b(7'b0111001));  // open: gt, eq, lt
  Comparator #(.width(7)) comparator_8 (.a(ASCII_code), .b(7'b0110110), .eq(plus_x0y));  // open: gt, lt
  Comparator #(.width(7), .value('h32)) comparator_9 (.a(ASCII_code), .b(7'b0110011), .eq(plus_x_y));  // open: gt, lt
  or or_1 (or_1_out, minus_x_y_t, _0x_y_t, plus_x_y_t);
  or or_2 (or_2_out, or_1_out, or_3_out);
  or or_3 (or_3_out, minus_x_y, _0x_y, plus_x_y);
  or or_4 (or_4_out, minus_x_y_t, minus_x0y, minus_x_y);
  or or_5 (or_5_out, or_4_out, or_6_out);
  or or_6 (or_6_out, plus_x_y_t, plus_x0y, plus_x_y);
  // Probe on counter_1_q
  Counter #(.width(5), .max('h1f)) counter_1 (
    .load(or_1_out), .count(or_2_out), .Q(counter_1_q), .clk(or_2_out));  // open: D, carry, clr
  // Probe on X
  Counter #(.width(5), .max('h1f)) counter_2 (
    .load(or_4_out), .count(or_5_out), .Q(X), .clk(or_5_out));  // open: D, carry, clr

  // Other names for the same wires on the sheet: _0x0y = Switch

  // Notes on the sheet:
  //   Y position
  //   X position
endmodule

module _32_bit_row_destructor (
  input  [31:0] Row,
  input  [4:0] Bit_selector,
  output [7:0] Selected_byte,
  output Selected_bit
);

  wire [31:1] shifter_2_out;
  wire [31:8] shifter_1_out;

  Shifter #(.width(32), .shift("lr")) shifter_1 (
    .in(Row), .\dist ({Bit_selector[4:3], 3'b000}), .out({shifter_1_out, Selected_byte}));
  Shifter #(.width(32), .shift("lr")) shifter_2 (
    .in({shifter_1_out, Selected_byte}), .\dist ({2'b00, Bit_selector[2:0]}),
    .out({shifter_2_out, Selected_bit}));
  Shifter #(.width(32), .shift("lr")) shifter_3 (
    .in({shifter_1_out, Selected_byte}), .\dist ({2'b00, Bit_selector[2:0]}),
    .out({shifter_2_out, Selected_bit}));
endmodule

module SELECT (
  input  [31:0] Input1,
  input  Input1_2,
  input  [31:0] Input2,
  output [31:0] Output
);

  Multiplexer #(.width(32), .disabled(0), .enable("false")) multiplexer_1 (
    .in0(Input1), .in1(Input2), .out(Output), .sel(Input1_2));
endmodule

module bit_invertor (
  input  [31:0] INPUT9,
  input  [31:0] INPUT1,
  input  [31:0] INPUT10,
  input  [31:0] INPUT17,
  input  [31:0] INPUT2,
  input  [31:0] INPUT31,
  input  [31:0] INPUT18,
  input  [31:0] INPUT25,
  input  [31:0] INPUT3,
  input  [31:0] INPUT12,
  input  [31:0] INPUT19,
  input  [31:0] INPUT26,
  input  [31:0] INPUT4,
  input  SWITCH,
  input  [31:0] INPUT13,
  input  [31:0] INPUT20,
  input  [31:0] INPUT27,
  input  [4:0] Y,
  input  [31:0] INPUT5,
  input  [4:0] X,
  input  [31:0] INPUT14,
  input  [31:0] INPUT21,
  input  [31:0] INPUT28,
  input  [31:0] INPUT6,
  input  [31:0] INPUT15,
  input  [31:0] INPUT22,
  input  [31:0] INPUT29,
  input  [31:0] INPUT7,
  input  [31:0] INPUT16,
  input  [31:0] INPUT23,
  input  [31:0] INPUT30,
  input  [31:0] INPUT8,
  input  [31:0] INPUT24,
  input  [31:0] INPUT31_2,
  output [31:0] CHANGED_STRING,
  output [31:0] OUTPUT1,
  output [31:0] OUTPUT2,
  output [31:0] OUTPUT3,
  output [31:0] OUTPUT4,
  output [31:0] OUTPUT5,
  output [31:0] OUTPUT6,
  output [31:0] OUTPUT7,
  output [31:0] OUTPUT8,
  output [31:0] OUTPUT9,
  output [31:0] OUTPUT10,
  output [31:0] OUTPUT11,
  output [31:0] OUTPUT12,
  output [31:0] OUTPUT13,
  output [31:0] OUTPUT14,
  output [31:0] OUTPUT15,
  output [31:0] OUTPUT16,
  output [31:0] OUTPUT17,
  output [31:0] OUTPUT17_2,
  output [31:0] OUTPUT18,
  output [31:0] OUTPUT19,
  output [31:0] OUTPUT20,
  output [31:0] OUTPUT21,
  output [31:0] OUTPUT22,
  output [31:0] OUTPUT23,
  output [31:0] OUTPUT24,
  output [31:0] OUTPUT25,
  output [31:0] OUTPUT26,
  output [31:0] OUTPUT27,
  output [31:0] OUTPUT28,
  output [31:0] OUTPUT29,
  output [31:0] OUTPUT30,
  output [31:0] OUTPUT31,
  output [31:0] OUTPUT32
);

  wire decoder_2_out0, decoder_2_out1, decoder_2_out2, decoder_2_out3, decoder_2_out4, decoder_2_out5,
       decoder_2_out6, decoder_2_out7, decoder_2_out8, decoder_2_out9, decoder_2_out10, decoder_2_out11,
       decoder_2_out12, decoder_2_out13, decoder_2_out14, decoder_2_out15, decoder_2_out16, decoder_2_out17,
       decoder_2_out18, decoder_2_out19, decoder_2_out20, decoder_2_out21, decoder_2_out22, decoder_2_out23,
       decoder_2_out24, decoder_2_out25, decoder_2_out26, decoder_2_out27, decoder_2_out28, decoder_2_out29,
       decoder_2_out30, decoder_2_out31;
  wire [31:0] decoder_1_out0, multiplexer_1_out, select_21_output, select_22_output, select_23_output,
       select_24_output, select_25_output, select_26_output, select_27_output, select_28_output,
       select_29_output, select_30_output, select_31_output, select_32_output, select_33_output,
       select_34_output, select_35_output, select_36_output, select_37_output, select_38_output,
       select_39_output, select_40_output, select_41_output, select_42_output, select_43_output,
       select_44_output, select_45_output, select_46_output, select_47_output, select_48_output,
       select_49_output, select_50_output, select_51_output, select_52_output, undriven, xor_1_out;

  SELECT select_1 (.Input1(INPUT1), .Input1_2(SWITCH), .Input2(select_21_output), .Output(OUTPUT1));
  SELECT select_2 (.Input1(INPUT2), .Input1_2(SWITCH), .Input2(select_22_output), .Output(OUTPUT2));
  SELECT select_3 (.Input1(INPUT3), .Input1_2(SWITCH), .Input2(select_23_output), .Output(OUTPUT3));
  SELECT select_4 (.Input1(INPUT4), .Input1_2(SWITCH), .Input2(select_24_output), .Output(OUTPUT4));
  SELECT select_5 (.Input1(INPUT5), .Input1_2(SWITCH), .Input2(select_25_output), .Output(OUTPUT5));
  SELECT select_6 (.Input1(INPUT6), .Input1_2(SWITCH), .Input2(select_26_output), .Output(OUTPUT6));
  SELECT select_7 (.Input1(INPUT7), .Input1_2(SWITCH), .Input2(select_27_output), .Output(OUTPUT7));
  SELECT select_8 (.Input1(INPUT8), .Input1_2(SWITCH), .Input2(select_28_output), .Output(OUTPUT8));
  SELECT select_9 (.Input1(INPUT9), .Input1_2(SWITCH), .Input2(select_29_output), .Output(OUTPUT9));
  SELECT select_10 (.Input1(INPUT10), .Input1_2(SWITCH), .Input2(select_30_output), .Output(OUTPUT10));
  SELECT select_11 (.Input1(INPUT31), .Input1_2(SWITCH), .Input2(select_31_output), .Output(OUTPUT11));
  Multiplexer #(.select(5), .width(32), .enable("false")) multiplexer_1 (
    .in0(INPUT1), .in1(INPUT2), .in2(INPUT3), .in3(INPUT4), .in4(INPUT5), .in5(INPUT6), .in6(INPUT7),
    .in7(INPUT8), .in8(INPUT9), .in9(INPUT10), .in10(INPUT31), .in11(INPUT12), .in12(INPUT13),
    .in13(INPUT14), .in14(INPUT15), .in15(INPUT16), .in16(INPUT17), .in17(INPUT18), .in18(INPUT19),
    .in19(INPUT20), .in20(INPUT21), .in21(INPUT22), .in22(INPUT23), .in23(INPUT24), .in24(INPUT25),
    .in25(INPUT26), .in26(INPUT27), .in27(INPUT28), .in28(INPUT29), .in29(INPUT30), .in30(INPUT31_2),
    .in31(undriven), .out(multiplexer_1_out), .sel(Y));
  SELECT select_12 (.Input1(INPUT12), .Input1_2(SWITCH), .Input2(select_32_output), .Output(OUTPUT12));
  Decoder #(.select(5), .disabled(0)) decoder_1 (
    .out0(decoder_1_out0[0]), .out1(decoder_1_out0[1]), .out2(decoder_1_out0[2]), .out3(decoder_1_out0[3]),
    .out4(decoder_1_out0[4]), .out5(decoder_1_out0[5]), .out6(decoder_1_out0[6]), .out7(decoder_1_out0[7]),
    .out8(decoder_1_out0[8]), .out9(decoder_1_out0[9]), .out10(decoder_1_out0[10]),
    .out11(decoder_1_out0[11]), .out12(decoder_1_out0[12]), .out13(decoder_1_out0[13]),
    .out14(decoder_1_out0[14]), .out15(decoder_1_out0[15]), .out16(decoder_1_out0[16]),
    .out17(decoder_1_out0[17]), .out18(decoder_1_out0[18]), .out19(decoder_1_out0[19]),
    .out20(decoder_1_out0[20]), .out21(decoder_1_out0[21]), .out22(decoder_1_out0[22]),
    .out23(decoder_1_out0[23]), .out24(decoder_1_out0[24]), .out25(decoder_1_out0[25]),
    .out26(decoder_1_out0[26]), .out27(decoder_1_out0[27]), .out28(decoder_1_out0[28]),
    .out29(decoder_1_out0[29]), .out30(decoder_1_out0[30]), .out31(decoder_1_out0[31]), .sel(X), .en(SWITCH));
  Decoder #(.select(5), .disabled(0)) decoder_2 (
    .out0(decoder_2_out0), .out1(decoder_2_out1), .out2(decoder_2_out2), .out3(decoder_2_out3),
    .out4(decoder_2_out4), .out5(decoder_2_out5), .out6(decoder_2_out6), .out7(decoder_2_out7),
    .out8(decoder_2_out8), .out9(decoder_2_out9), .out10(decoder_2_out10), .out11(decoder_2_out11),
    .out12(decoder_2_out12), .out13(decoder_2_out13), .out14(decoder_2_out14), .out15(decoder_2_out15),
    .out16(decoder_2_out16), .out17(decoder_2_out17), .out18(decoder_2_out18), .out19(decoder_2_out19),
    .out20(decoder_2_out20), .out21(decoder_2_out21), .out22(decoder_2_out22), .out23(decoder_2_out23),
    .out24(decoder_2_out24), .out25(decoder_2_out25), .out26(decoder_2_out26), .out27(decoder_2_out27),
    .out28(decoder_2_out28), .out29(decoder_2_out29), .out30(decoder_2_out30), .out31(decoder_2_out31),
    .sel(Y), .en(SWITCH));
  SELECT select_13 (.Input1(INPUT13), .Input1_2(SWITCH), .Input2(select_33_output), .Output(OUTPUT13));
  SELECT select_14 (.Input1(INPUT14), .Input1_2(SWITCH), .Input2(select_34_output), .Output(OUTPUT14));
  assign xor_1_out = multiplexer_1_out ^ decoder_1_out0;  // XOR_Gate xor_1, 32 bits wide
  SELECT select_15 (.Input1(INPUT15), .Input1_2(SWITCH), .Input2(select_35_output), .Output(OUTPUT15));
  SELECT select_16 (.Input1(INPUT17), .Input1_2(SWITCH), .Input2(select_37_output), .Output(OUTPUT17));
  SELECT select_17 (.Input1(multiplexer_1_out), .Input1_2(SWITCH), .Input2(xor_1_out), .Output(CHANGED_STRING));
  SELECT select_18 (.Input1(INPUT18), .Input1_2(SWITCH), .Input2(select_38_output), .Output(OUTPUT18));
  SELECT select_19 (.Input1(INPUT19), .Input1_2(SWITCH), .Input2(select_39_output), .Output(OUTPUT19));
  SELECT select_20 (.Input1(INPUT20), .Input1_2(SWITCH), .Input2(select_40_output), .Output(OUTPUT20));
  SELECT select_21 (.Input1(INPUT1), .Input1_2(decoder_2_out0), .Input2(xor_1_out), .Output(select_21_output));
  SELECT select_22 (.Input1(INPUT2), .Input1_2(decoder_2_out1), .Input2(xor_1_out), .Output(select_22_output));
  SELECT select_23 (.Input1(INPUT3), .Input1_2(decoder_2_out2), .Input2(xor_1_out), .Output(select_23_output));
  SELECT select_24 (.Input1(INPUT4), .Input1_2(decoder_2_out3), .Input2(xor_1_out), .Output(select_24_output));
  SELECT select_25 (.Input1(INPUT5), .Input1_2(decoder_2_out4), .Input2(xor_1_out), .Output(select_25_output));
  SELECT select_26 (.Input1(INPUT6), .Input1_2(decoder_2_out5), .Input2(xor_1_out), .Output(select_26_output));
  SELECT select_27 (.Input1(INPUT7), .Input1_2(decoder_2_out6), .Input2(xor_1_out), .Output(select_27_output));
  SELECT select_28 (.Input1(INPUT8), .Input1_2(decoder_2_out7), .Input2(xor_1_out), .Output(select_28_output));
  SELECT select_29 (.Input1(INPUT9), .Input1_2(decoder_2_out8), .Input2(xor_1_out), .Output(select_29_output));
  SELECT select_30 (.Input1(INPUT10), .Input1_2(decoder_2_out9), .Input2(xor_1_out), .Output(select_30_output));
  SELECT select_31 (.Input1(INPUT31), .Input1_2(decoder_2_out10), .Input2(xor_1_out), .Output(select_31_output));
  SELECT select_32 (.Input1(INPUT12), .Input1_2(decoder_2_out11), .Input2(xor_1_out), .Output(select_32_output));
  SELECT select_33 (.Input1(INPUT13), .Input1_2(decoder_2_out12), .Input2(xor_1_out), .Output(select_33_output));
  SELECT select_34 (.Input1(INPUT14), .Input1_2(decoder_2_out13), .Input2(xor_1_out), .Output(select_34_output));
  SELECT select_35 (.Input1(INPUT15), .Input1_2(decoder_2_out14), .Input2(xor_1_out), .Output(select_35_output));
  SELECT select_36 (.Input1(INPUT16), .Input1_2(decoder_2_out15), .Input2(xor_1_out), .Output(select_36_output));
  SELECT select_37 (.Input1(INPUT17), .Input1_2(decoder_2_out16), .Input2(xor_1_out), .Output(select_37_output));
  SELECT select_38 (.Input1(INPUT18), .Input1_2(decoder_2_out17), .Input2(xor_1_out), .Output(select_38_output));
  SELECT select_39 (.Input1(INPUT19), .Input1_2(decoder_2_out18), .Input2(xor_1_out), .Output(select_39_output));
  SELECT select_40 (.Input1(INPUT20), .Input1_2(decoder_2_out19), .Input2(xor_1_out), .Output(select_40_output));
  SELECT select_41 (.Input1(INPUT21), .Input1_2(decoder_2_out20), .Input2(xor_1_out), .Output(select_41_output));
  SELECT select_42 (.Input1(INPUT22), .Input1_2(decoder_2_out21), .Input2(xor_1_out), .Output(select_42_output));
  SELECT select_43 (.Input1(INPUT23), .Input1_2(decoder_2_out22), .Input2(xor_1_out), .Output(select_43_output));
  SELECT select_44 (.Input1(INPUT24), .Input1_2(decoder_2_out23), .Input2(xor_1_out), .Output(select_44_output));
  SELECT select_45 (.Input1(INPUT25), .Input1_2(decoder_2_out24), .Input2(xor_1_out), .Output(select_45_output));
  SELECT select_46 (.Input1(INPUT26), .Input1_2(decoder_2_out25), .Input2(xor_1_out), .Output(select_46_output));
  SELECT select_47 (.Input1(INPUT27), .Input1_2(decoder_2_out26), .Input2(xor_1_out), .Output(select_47_output));
  SELECT select_48 (.Input1(INPUT28), .Input1_2(decoder_2_out27), .Input2(xor_1_out), .Output(select_48_output));
  SELECT select_49 (.Input1(INPUT29), .Input1_2(decoder_2_out28), .Input2(xor_1_out), .Output(select_49_output));
  SELECT select_50 (.Input1(INPUT30), .Input1_2(decoder_2_out29), .Input2(xor_1_out), .Output(select_50_output));
  SELECT select_51 (.Input1(INPUT31_2), .Input1_2(decoder_2_out30), .Input2(xor_1_out), .Output(select_51_output));
  SELECT select_52 (.Input1(undriven), .Input1_2(decoder_2_out31), .Input2(xor_1_out), .Output(select_52_output));
  SELECT select_53 (.Input1(INPUT21), .Input1_2(SWITCH), .Input2(select_41_output), .Output(OUTPUT21));
  SELECT select_54 (.Input1(INPUT22), .Input1_2(SWITCH), .Input2(select_42_output), .Output(OUTPUT22));
  SELECT select_55 (.Input1(INPUT23), .Input1_2(SWITCH), .Input2(select_43_output), .Output(OUTPUT23));
  SELECT select_56 (.Input1(INPUT24), .Input1_2(SWITCH), .Input2(select_44_output), .Output(OUTPUT24));
  SELECT select_57 (.Input1(INPUT25), .Input1_2(SWITCH), .Input2(select_45_output), .Output(OUTPUT25));
  SELECT select_58 (.Input1(INPUT26), .Input1_2(SWITCH), .Input2(select_46_output), .Output(OUTPUT26));
  SELECT select_59 (.Input1(INPUT27), .Input1_2(SWITCH), .Input2(select_47_output), .Output(OUTPUT27));
  SELECT select_60 (.Input1(INPUT28), .Input1_2(SWITCH), .Input2(select_48_output), .Output(OUTPUT28));
  SELECT select_61 (.Input1(INPUT29), .Input1_2(SWITCH), .Input2(select_49_output), .Output(OUTPUT29));
  SELECT select_62 (.Input1(INPUT30), .Input1_2(SWITCH), .Input2(select_50_output), .Output(OUTPUT30));
  SELECT select_63 (.Input1(INPUT31_2), .Input1_2(SWITCH), .Input2(select_51_output), .Output(OUTPUT31));
  SELECT select_64 (.Input1(INPUT31_2), .Input1_2(SWITCH), .Input2(select_51_output), .Output(OUTPUT31));
  SELECT select_65 (.Input1(undriven), .Input1_2(SWITCH), .Input2(select_52_output), .Output(OUTPUT32));

  assign OUTPUT17_2 = OUTPUT17;
endmodule

module row_reverser (
  input  [31:0] row,
  output [31:0] reversed_row
);


  assign reversed_row = {row[0], row[1], row[2], row[3], row[4], row[5], row[6], row[7], row[8], row[9], row[10], row[11], row[12], row[13], row[14], row[15], row[16], row[17], row[18], row[19], row[20], row[21], row[22], row[23], row[24], row[25], row[26], row[27], row[28], row[29], row[30], row[31]};
endmodule
